// Logisim project CPU.circ as structural Verilog: 1 circuit, main circuit main
module main (
);

  wire K0, K1, K2, K3, L8, L9, S0, S1, S2, S3, S4, S5, S6, S7, S8, S9;
  wire [3:0] HEX0, HEX1, HEX2, HEX3, HEX4, HEX5;
  wire [7:0] BAR_END;

  Hex_Digit_Display hex_digit_display_1 (.value(HEX5));  // open: dp
  LED u_L9 (.in(L9));
  LED u_L8 (.in(L8));
  // DipSwitch #(.NSwitches(1)) S9: pin names not known; wires that end beside it: S9
  // DipSwitch #(.NSwitches(1)) S8: pin names not known; wires that end beside it: S8
  // Digital_Oscilloscope #(.nState(16)) digital_oscilloscope_1: pin names not known; wires that end beside it: S9, BAR_END[0], BAR_END[1], BAR_END[2], BAR_END[3], BAR_END[4], BAR_END[5], BAR_END[6], BAR_END[7], S0
  Hex_Digit_Display hex_digit_display_2 (.value(HEX3));  // open: dp
  Hex_Digit_Display hex_digit_display_3 (.value(HEX4));  // open: dp
  LED L6 (.in(BAR_END[6]));
  LED L5 (.in(BAR_END[5]));
  LED L7 (.in(BAR_END[7]));
  // DipSwitch #(.NSwitches(1)) S6: pin names not known; wires that end beside it: S6
  // DipSwitch #(.NSwitches(1)) S5: pin names not known; wires that end beside it: S5
  // DipSwitch #(.NSwitches(1)) S7: pin names not known; wires that end beside it: S7
  Hex_Digit_Display hex_digit_display_4 (.value(HEX2));  // open: dp
  LED L3 (.in(BAR_END[3]));
  LED L4 (.in(BAR_END[4]));
  // DipSwitch #(.NSwitches(1)) S2: pin names not known; wires that end beside it: S2
  // DipSwitch #(.NSwitches(1)) S4: pin names not known; wires that end beside it: S4
  // DipSwitch #(.NSwitches(1)) S3: pin names not known; wires that end beside it: S3
  Hex_Digit_Display hex_digit_display_5 (.value(HEX0));  // open: dp
  Hex_Digit_Display hex_digit_display_6 (.value(HEX1));  // open: dp
  LED L2 (.in(BAR_END[2]));
  LED L0 (.in(BAR_END[0]));
  LED L1 (.in(BAR_END[1]));
  // DipSwitch #(.NSwitches(1)) S1: pin names not known; wires that end beside it: S1
  // DipSwitch #(.NSwitches(1)) S0: pin names not known; wires that end beside it: S0
  Button u_K2 (.out(K2));
  Button u_K3 (.out(K3));
  Button u_K1 (.out(K1));
  Button u_K0 (.out(K0));
  ROM #(.dataWidth(16), .Select("low")) rom_1 (.addr(BAR_END), .data({HEX5, HEX4, HEX3, HEX2}));
  // contador8bits contador8bits_1: pin names not known; wires that end beside it: 1'b0, S9, 1'b1, BAR_END[0], S0, BAR_END[1], BAR_END[2], BAR_END[3], BAR_END[4], BAR_END[5], BAR_END[6], BAR_END[7]

  // Other names for the same wires on the sheet: L0 = BAR_END[0]; L1 = BAR_END[1]; L2 = BAR_END[2]; L3 = BAR_END[3];
  //   L4 = BAR_END[4]; L5 = BAR_END[5]; L6 = BAR_END[6]; L7 = BAR_END[7]; ULA[1:0] = HEX4[1:0]; JMP[1:0] = HEX4[3:2];
  //   RgIN[1:0] = HEX5[1:0]; RgTO[1:0] = HEX5[3:2]

  // Notes on the sheet:
  //   contents of rom_1 (hex, n*v repeats v):
  //   110 0 0 101 1001 1 0 1 110 10 0 10 110 11 0 100 0 1100 0 1000 13*0 100 0 0 110 0 0 1 1001 0 0 1 1001
  //   0 0 10 110 11 0 10 110 1 0 10 1001 11 0 10 110 10 0 0 110 0 0 1 0 1000
endmodule
