// Logisim project biblioteca.circ as structural Verilog
module contador8bits (
  input  CLR,
  input  CLK,
  input  E,
  input  [3:0] JMP_Operando,
  input  JMP,
  output Q0,
  output Q1,
  output Q2,
  output Q3,
  output Q4,
  output Q5,
  output Q6,
  output Q7
);

  wire and_1_out, and_2_out, and_3_out, and_4_out, and_5_out, and_6_out, and_7_out, and_8_out, and_9_out,
       and_10_out, and_11_out, and_12_out, and_13_out, and_14_out, or_1_out, or_2_out, or_3_out, or_4_out;

  and and_1 (and_1_out, JMP, ~JMP_Operando[0]);  // AND_Gate
  or or_1 (or_1_out, and_1_out, CLR);
  T_Flip_Flop #(.Pre_Clr_Positions("BELOW_ABOVE")) t_ff_1 (
    .clk(CLK), .T(E), .Q(Q0), .preset(and_2_out), .reset(or_1_out));  // open: Qn
  and and_2 (and_2_out, JMP, JMP_Operando[0]);
  and and_3 (and_3_out, JMP, ~JMP_Operando[1]);  // AND_Gate
  or or_2 (or_2_out, and_3_out, CLR);
  and and_4 (and_4_out, JMP, JMP_Operando[1]);
  T_Flip_Flop #(.Pre_Clr_Positions("BELOW_ABOVE")) t_ff_2 (
    .clk(CLK), .T(Q0), .Q(Q1), .preset(and_4_out), .reset(or_2_out));  // open: Qn
  and and_5 (and_5_out, Q0, Q1);
  and and_6 (and_6_out, JMP, ~JMP_Operando[2]);  // AND_Gate
  or or_3 (or_3_out, and_6_out, CLR);
  and and_7 (and_7_out, JMP, JMP_Operando[2]);
  T_Flip_Flop #(.Pre_Clr_Positions("BELOW_ABOVE")) t_ff_3 (
    .clk(CLK), .T(and_5_out), .Q(Q2), .preset(and_7_out), .reset(or_3_out));  // open: Qn
  and and_8 (and_8_out, and_5_out, Q2);
  and and_9 (and_9_out, JMP, ~JMP_Operando[3]);  // AND_Gate
  or or_4 (or_4_out, and_9_out, CLR);
  T_Flip_Flop #(.Pre_Clr_Positions("BELOW_ABOVE")) t_ff_4 (
    .clk(CLK), .T(and_8_out), .Q(Q3), .preset(and_10_out), .reset(or_4_out));  // open: Qn
  and and_10 (and_10_out, JMP, JMP_Operando[3]);
  and and_11 (and_11_out, and_8_out, Q3);
  T_Flip_Flop #(.Pre_Clr_Positions("BELOW_ABOVE")) t_ff_5 (
    .clk(CLK), .T(and_11_out), .Q(Q4), .preset(1'b0), .reset(JMP));  // open: Qn
  and and_12 (and_12_out, and_11_out, Q4);
  T_Flip_Flop #(.Pre_Clr_Positions("BELOW_ABOVE")) t_ff_6 (
    .clk(CLK), .T(and_12_out), .Q(Q5), .preset(1'b0), .reset(JMP));  // open: Qn
  and and_13 (and_13_out, and_12_out, Q5);
  T_Flip_Flop #(.Pre_Clr_Positions("BELOW_ABOVE")) t_ff_7 (
    .clk(CLK), .T(and_13_out), .Q(Q6), .preset(1'b0), .reset(JMP));  // open: Qn
  and and_14 (and_14_out, and_13_out, Q6);
  T_Flip_Flop #(.Pre_Clr_Positions("BELOW_ABOVE")) t_ff_8 (
    .clk(CLK), .T(and_14_out), .Q(Q7), .preset(1'b0), .reset(JMP));  // open: Qn

  // Other names for the same wires on the sheet: _0 = JMP_Operando[0]; _1 = JMP_Operando[1]; _2 = JMP_Operando[2];
  //   _3 = JMP_Operando[3]
endmodule

module registrador4bits (
  input  Eclock,
  input  D1,
  input  D2,
  input  D3,
  input  D4,
  output Q1,
  output Q2,
  output Q3,
  output Q4
);

  D_Flip_Flop d_ff_1 (.clk(Eclock), .D(D1), .Q(Q1));  // open: Qn, preset, reset
  D_Flip_Flop d_ff_2 (.clk(Eclock), .D(D2), .Q(Q2));  // open: Qn, preset, reset
  D_Flip_Flop d_ff_3 (.clk(Eclock), .D(D3), .Q(Q3));  // open: Qn, preset, reset
  D_Flip_Flop d_ff_4 (.clk(Eclock), .D(D4), .Q(Q4));  // open: Qn, preset, reset
endmodule

module unidade_controle (
  input  [1:0] JMP,
  output \Operaçao_de_ULA ,
  output Reinicia_Registradores,
  output Reinicia_Contador,
  output JMP_Para_Operando
);

  Demultiplexer #(.select(2), .enable("false")) demultiplexer_1 (
    .out0(\Operaçao_de_ULA ), .out1(Reinicia_Registradores), .out2(Reinicia_Contador),
    .out3(JMP_Para_Operando), .in(1'b1), .sel(JMP));
endmodule
